# Fritzing sketch BarBot (saved by Fritzing 0.9.3b)
circuit board: 8.46667cm x 5.64444cm
breadboards: 1

parts:
  IC1 = ADPDRRT005PG2A5 [package="DIP (Dual Inline) [THT]"]
  Raspberry_Pi_1 = Raspberry Pi 3 [part_number=RPI-3-V1.2]
  C1 = Ceramic Capacitor [capacitance=100nF package="100 mil [THT, multilayer]"]
  Part1 = HX711 Weighing Sensor Module
  PWM1 = PCA9685 16x12-bit PWM Breakout

nets:
  GND: IC1.pin1, Raspberry_Pi_1.GND, C1.1, Part1.GND, PWM1.no_name_yet#501
  3V3: IC1.pin2, Raspberry_Pi_1.3v3, C1.0, Part1.VCC, PWM1.no_name_yet#506
  N1: IC1.pin5, Raspberry_Pi_1.GPIO2, PWM1.no_name_yet#504
  N2: IC1.pin6, Raspberry_Pi_1.GPIO3, PWM1.no_name_yet#503
  N3: Raspberry_Pi_1.GIPO10, Part1.CK/TX
  N4: Raspberry_Pi_1.GIPO9, Part1.DO/RX

notes:
  CK / TX connected to MOSI

custom parts:
  ADPDRRT005PG2A5: I2C Pressure Sensor
